# Fritzing sketch Schematics (saved by Fritzing 0.9.3b)
circuit board: 21.7491cm x 13.7176cm
breadboards: 1

parts:
  Arduino_Nano = Arduino Nano (Rev3.0)
  Red = Rotary Potentiometer (Small) [maximum_resistance=10kΩ package=THT]
  Green = Rotary Potentiometer (Small) [maximum_resistance=10kΩ package=THT]
  Blue = Rotary Potentiometer (Small) [maximum_resistance=10kΩ package=THT]
  R1 = Resistor [tolerance=±5% resistance=1k package=THT]
  R2 = Resistor [tolerance=±5% resistance=1k package=THT]
  R3 = Resistor [tolerance=±5% resistance=1k package=THT]
  LCD = LCD-16X2 [package=lcd-16x2_nosilk]
  LCD_16x2_i2c_Module = LCM1602 IIC [part_number=I2C chip_label="LCM1602 IIC" package="DIP (Dual Inline) [THT]"]
  Button = Round Pushbutton
  Q1 = TIP120 Hi-Current Darlington Transistor
  Q3 = TIP120 Hi-Current Darlington Transistor
  RGB_Strip = RGB Strip LED
  Q2 = TIP120 Hi-Current Darlington Transistor
  part = DC Power [voltage=5V]
  part_2 = DC Power [voltage=12V]

nets:
  GND: Arduino_Nano.GND, Red.leg2, Green.leg2, Blue.leg2, LCD_16x2_i2c_Module.GND, Button.leg1, Q1.EMITTER, Q3.EMITTER, Q2.EMITTER, part.V-, part_2.V-
  N1: Arduino_Nano.D7, Button.leg0
  N2: Arduino_Nano.D9, R1.Pin_0
  N3: Arduino_Nano.D10, R2.Pin_0
  N4: Arduino_Nano.D11/MOSI, R3.Pin_0
  N5: Arduino_Nano.VIN, part.V+
  5V: Arduino_Nano.5V, Red.leg1, Green.leg1, Blue.leg1, LCD_16x2_i2c_Module.VCC
  N6: Arduino_Nano.A5, LCD_16x2_i2c_Module.SCL
  N7: Arduino_Nano.A4, LCD_16x2_i2c_Module.SDA
  N8: Arduino_Nano.A2, Blue.wiper
  N9: Arduino_Nano.A1, Green.wiper
  N10: Arduino_Nano.A0, Red.wiper
  N11: R1.Pin_1, Q1.BASE
  N12: R2.Pin_1, Q2.BASE
  N13: R3.Pin_1, Q3.BASE
  VSS: LCD.VSS, LCD_16x2_i2c_Module.VSS
  VDD: LCD.VDD, LCD_16x2_i2c_Module.VDD
  N14: LCD.VO, LCD_16x2_i2c_Module.V0
  N15: LCD.RS, LCD_16x2_i2c_Module.RS
  N16: LCD.R_W, LCD_16x2_i2c_Module.RW
  N17: LCD.E, LCD_16x2_i2c_Module.E
  N18: LCD.DB0, LCD_16x2_i2c_Module.D0
  N19: LCD.DB1, LCD_16x2_i2c_Module.D1
  N20: LCD.DB2, LCD_16x2_i2c_Module.D2
  N21: LCD.DB3, LCD_16x2_i2c_Module.D3
  N22: LCD.DB4, LCD_16x2_i2c_Module.D4
  N23: LCD.DB5, LCD_16x2_i2c_Module.D5
  N24: LCD.DB6, LCD_16x2_i2c_Module.D6
  N25: LCD.DB7, LCD_16x2_i2c_Module.D7
  N26: LCD.A, LCD_16x2_i2c_Module.A
  N27: LCD.K, LCD_16x2_i2c_Module.K
  N28: LCD_16x2_i2c_Module.LED_A, LCD_16x2_i2c_Module.LED_B
  N29: Q1.COLLECTOR, RGB_Strip.Red_Connect
  N30: Q3.COLLECTOR, RGB_Strip.Blue_Connect
  N31: RGB_Strip.Common_Connect, part_2.V+
  N32: RGB_Strip.Green_Connect, Q2.COLLECTOR

notes:
  Vin -> 5v
  Gnd -> Gnd
  RGB + -> 12v

custom parts:
  LCM1602 IIC: I2C-Module to use a 1602 or 2004 LCD on with the wire.h libory Serial LCD Modul
  RGB Strip LED: A tri-color Strip LED with red, green and blue. Based on LED SMD 5050 RGB Pin order: common cathode - green - red - blue

// code stored in the sketch: pcLedControl.ino
#include <Wire.h>
#include <LiquidCrystal_I2C.h>
#define red 9
#define green 10
#define blue 11
#define button 7
int mode = 1;
const int maxMode = 2;
int d = 50;
int rgb[] = {000, 000, 000};
int i = 0;
int j = 0;
int val;
const char *zeroes[] = {"", "0", "00", "000"};
const char *animation1[] = {"*RGB CONTROLLER*", "GB CONTROLLER*:)", " CONTROLLER*:)IL", "ONTROLLER*:)ILIO", "TROLLER*:)ILIOPO", "OLLER*:)ILIOPOUL", "LER*:)ILIOPOULOS", "R*:)ILIOPOULOS(:", " :)ILIOPOULOS(: ", "ILIOPOULOS(:*RGB", "IOPOULOS(:*RGB C", "POULOS(:*RGB CON", "ULOS(:*RGB CONTR", "OS(:*RGB CONTROL"};
const char *animation2[] = {" RGB CONTROLLER ", "  MANUAL  MODE  "};
const int animLen = 2;
int curAnim = 0;
const int animD = 2000;
int passedD = animD;
const int minVal = 2;
const int wheelDelay = 10;
const float breathPercentage = 0.98;
const int breathDelay = 50;

LiquidCrystal_I2C lcd = LiquidCrystal_I2C(0x27, 16, 2);
void setup()
{
  for (i = 0; i < 3; i++);
  {
    pinMode("A" + i, INPUT);
  }
  pinMode(red, OUTPUT);
  pinMode(green, OUTPUT);
  pinMode(blue, OUTPUT);
  pinMode(button, INPUT_PULLUP);
  lcd.init();
  lcd.backlight();
  lcd.setCursor(1, 0);
  lcd.print("System Booting");
  lcd.setCursor(1, 1);
  lcd.print("RGB CONTROLLER");
  delay(2000);
  Serial.begin(9600);
}
void loop()
{
  if (digitalRead(button) == LOW)
  {
    if (mode < maxMode)
    {
      mode++;

    }
    else
    {
      mode = 0;
    }

    for (int i = 0; i < 2; i++)
    {
      analogWrite(red, 255);
      analogWrite(green, 0);
      analogWrite(blue, 0);
      delay(500);
      analogWrite(red, 0);
      delay(500);
    }
  }

  if (mode == 0)
  {
    manual();
  }
  else if (mode == 1)
  {
    breath();
  }
  else if (mode == 2)
  {
    colorWheel();
  }
}

void colorWheel()
{

  for (/* no initialization */; rgb[0] >= 0, rgb[2] < 255; rgb[2]++, rgb[0]--) /*red -> blue*/
  {
    for (int j = 0; j < 3; j++)
    {
      if (rgb[j] < 0)
      {
        rgb[j] = 0;
      }
      else if (rgb[j] > 255)
      {
        rgb[j] = 255;
      }
    }
    analogWrite(red, rgb[0]);
    analogWrite(blue, rgb[2]);
    delay(wheelDelay);
    if (digitalRead(button) == LOW)
    {
      break;
    }
  }

  for (/* no initialization */; rgb[2] >= 0, rgb[1] < 255; rgb[1]++, rgb[2]--) /*blue -> green*/

  {
    for (int j = 0; j < 3; j++)
    {
      if (rgb[j] < 0)
      {
        rgb[j] = 0;
      }
      else if (rgb[j] > 255)
      {
        rgb[j] = 255;
      }
    }
    analogWrite(blue, rgb[2]);
    analogWrite(green, rgb[1]);
    delay(wheelDelay);
    if (digitalRead(button) == LOW)
    {
      break;
    }
  }

  for (/* no initialization */; rgb[1] >= 0, rgb[0] < 255; rgb[0]++, rgb[1]--) /*green -> red*/

  {
    for (int j = 0; j < 3; j++)
    {
      if (rgb[j] < 0)
      {
        rgb[j] = 0;
      }
      else if (rgb[j] > 255)
      {
        rgb[j] = 255;
      }
    }
    analogWrite(red, rgb[0]);
    analogWrite(green, rgb[1]);
    delay(wheelDelay);
    if (digitalRead(button) == LOW)
    {
      break;
    }


  }
}

void manual()
{
  if (passedD >= animD)
  {
    if (curAnim >= animLen)
    {
      curAnim = 0;
    }
    lcd.setCursor(0, 0);
    lcd.print(animation2[curAnim]);
    curAnim ++;
    passedD = 0;
  }
  else
  {
    passedD += d;
  }
  valRead();
  lcd.setCursor(1, 1);
  lcd.print("R" + String(zeroes[3 - (String(rgb[0]).length())] + String(rgb[0])) + " G" + String(zeroes[3 - (String(rgb[1]).length())] + String(rgb[1])) + " B" + String(zeroes[3 - (String(rgb[2]).length())] + String(rgb[2])));
  analogWrite(red, rgb[0]);
  analogWrite(green, rgb[1]);
  analogWrite(blue, rgb[2]);
  delay(d);
}

void breath()
{
  valRead();
  analogWrite(red, rgb[0]);
  analogWrite(green, rgb[1]);
  analogWrite(blue, rgb[2]);
  int beforeRGB[] = {rgb[0], rgb[1], rgb[2]};
  int previousRGB[] = {0, 0, 0};
  while (rgb[0] > 0 || rgb[1] > 0 || rgb[2] > 0)
  {
    for (int j = 0; j < 3; j++)
    {

      if (digitalRead(button) == LOW)
      {
        break;
      }
      if (rgb[j] > 0)
      {
        rgb[j] = round(rgb[j] * 0.9);
        if (rgb[j] == previousRGB[j])
        {
          rgb[j]--;
        }
        previousRGB[j] = rgb[j];
      }
      else
      {
        rgb[j] = 0;
      }

      if (rgb[j] < 0)
      {
        rgb[j] = 0;
      }
      else if (rgb[j] > 255)
      {
        rgb[j] = 255;
      }
    }
    analogWrite(red, rgb[0]);
    analogWrite(green, rgb[1]);
    analogWrite(blue, rgb[2]);
    if (digitalRead(button) == LOW)
    {
      break;
    }
    delay(breathDelay);
    //for (int i = maxRGB; i > 0; i--)
  }
  delay(150);

  previousRGB[0] = -1;
  previousRGB[1] = -1;
  previousRGB[2] = -2;
  while (rgb[0] < beforeRGB[0] || rgb[1] < beforeRGB[1] || rgb[2] < beforeRGB[2])
  {
    for (int j = 0; j < 3; j++)
    {
      if (digitalRead(button) == LOW)
      {
        break;
      }
      if (beforeRGB[j] != 0 && rgb[j] < beforeRGB[j] && rgb[j] < 255)
      {
        rgb[j] = round((rgb[j] * 1.1) + 0.3);
        if (rgb[j] == previousRGB[j])
        {
          rgb[j]++;
        }

        previousRGB[j] = rgb[j];
      }
      else
      {
        rgb[j] = beforeRGB[j];
      }
      if (rgb[j] < 0)
      {
        rgb[j] = 0;
      }
      else if (rgb[j] > 255)
      {
        rgb[j] = 255;
      }
    }
    analogWrite(red, rgb[0]);
    analogWrite(green, rgb[1]);
    analogWrite(blue, rgb[2]);
    if (digitalRead(button) == LOW)
    {
      break;
    }
    delay(breathDelay);
  }
  delay(1500);
}

void valRead()
{
  val = map(analogRead(A0), 0, 1023, 255, 0);
  if (val >= minVal)
  {
    rgb[0] = val;
  }
  else
  {
    rgb[0] = 0;
  }
  val = map(analogRead(A1), 0, 1023, 255, 0);
  if (val >= minVal)
  {
    rgb[1] = val;
  }
  else
  {
    rgb[1] = 0;
  }
  val = map(analogRead(A2), 0, 1023, 255, 0);
  if (val >= minVal)
  {
    rgb[2] = val;
  }
  else
  {
    rgb[2] = 0;
  }
}

// code stored in the sketch: PcRGB_all.ino
//import required libraries
#include <Wire.h>
#include <LiquidCrystal_I2C.h>

//LCD initialisation 
LiquidCrystal_I2C lcd = LiquidCrystal_I2C(0x27, 16, 2);

//define pins for RGB values output and button
#define red 9
#define green 10
#define blue 11
#define button 7

//define loop variables to use them later inside loops
int i = 0;
int j = 0;

//define variables for mode selection
const int maxMode = 2; //if you add/remove a mode increase/decrease this value
int mode = 0; //By changing this value you change on which mode the controller will start

//define variables for LCD display and animation
const char *zeroes[] = {"", "0", "00", "000"};
const char *animation[] = {" RGB CONTROLLER ", "  MANUAL  MODE  "};//you can add an extra animation with a different name but you should change the name in line 198 and the animation length accordingly
const int animLen = 2;//enter the length of your animation starting counting from 1
const int maxAnimD = 2000;
int anim_delay = 50;
int curAnim = 0;
int passedD = maxAnimD;

//define variables for reading RGB values from potentiometer
const int minVal = 2; //below this value 0 is returned as reading
int val; //temporarily stores read vealues
int rgb[] = {000, 000, 000};

//define variables for wheel and breath animations
const float breathPercentage = 0.98; //percentage to increase/decrease breathing smoothness
const int wheelDelay = 10;
const int breathDelay = 50;

void setup()
{
  //set analog pins 1-3 as inputs for the potentiometers
  for (i = 0; i < 3; i++);
  {
    pinMode("A" + i, INPUT);
  }

  //same for digital pins for RGB outputs and button
  pinMode(red, OUTPUT);
  pinMode(green, OUTPUT);
  pinMode(blue, OUTPUT);
  pinMode(button, INPUT_PULLUP);
  
  //LCD initialisation
  lcd.init();
  lcd.backlight();
  lcd.setCursor(0, 0);
  lcd.print(" Your name here ");
  lcd.setCursor(1, 1);
  lcd.print("RGB CONTROLLER");
  delay(2000);
}
void loop()
{
  //change mode if button pressed
  if (digitalRead(button) == LOW)
  {
    //loop through modes
    if (mode < maxMode)
    {
      mode++;

    }
    else
    {
      mode = 0;
    }

    //signal for mode change
    for (int i = 0; i < 2; i++)
    {
      analogWrite(red, 255);
      analogWrite(green, 0);
      analogWrite(blue, 0);
      delay(500);
      analogWrite(red, 0);
      delay(500);
    }
  }

  //go to selected mode
  if (mode == 0)
  {
    manual();
  }
  else if (mode == 1)
  {
    breath();
  }
  else if (mode == 2)
  {
    colorWheel();
  }
}

//loop through colors (rainbow effect)
void colorWheel()
{
  for (/* no initialization */; rgb[0] >= 0, rgb[2] < 255; rgb[2]++, rgb[0]--) /*red -> blue*/
  {
    for (int j = 0; j < 3; j++)
    {
      if (rgb[j] < 0)
      {
        rgb[j] = 0;
      }
      else if (rgb[j] > 255)
      {
        rgb[j] = 255;
      }
    }
    
    //output RGB values
    analogWrite(red, rgb[0]);
    analogWrite(blue, rgb[2]);
    delay(wheelDelay);

    //test for mode button press
    if (digitalRead(button) == LOW)
    {
      break;
    }
  }

  for (/* no initialization */; rgb[2] >= 0, rgb[1] < 255; rgb[1]++, rgb[2]--) /*blue -> green*/

  {
    for (int j = 0; j < 3; j++)
    {
      if (rgb[j] < 0)
      {
        rgb[j] = 0;
      }
      else if (rgb[j] > 255)
      {
        rgb[j] = 255;
      }
    }
    analogWrite(blue, rgb[2]);
    analogWrite(green, rgb[1]);
    delay(wheelDelay);
    if (digitalRead(button) == LOW)
    {
      break;
    }
  }

  for (/* no initialization */; rgb[1] >= 0, rgb[0] < 255; rgb[0]++, rgb[1]--) /*green -> red*/

  {
    for (int j = 0; j < 3; j++)
    {
      if (rgb[j] < 0)
      {
        rgb[j] = 0;
      }
      else if (rgb[j] > 255)
      {
        rgb[j] = 255;
      }
    }
    analogWrite(red, rgb[0]);
    analogWrite(green, rgb[1]);
    delay(wheelDelay);
    if (digitalRead(button) == LOW)
    {
      break;
    }


  }
}

//changes the color based on the potentiometer input
void manual()
{
  //animation frame change
  if (passedD >= maxAnimD)
  {
    if (curAnim >= animLen)
    {
      curAnim = 0;
    }

    //show animation frame on LCD
    lcd.setCursor(0, 0);
    lcd.print(animation[curAnim]);
    curAnim ++;
    passedD = 0;
  }
  else
  {
    passedD += anim_delay;
  }

  //read values
  valRead();

  //write values to LCD
  lcd.setCursor(1, 1);
  lcd.print("R" + String(zeroes[3 - (String(rgb[0]).length())] + String(rgb[0])) + " G" + String(zeroes[3 - (String(rgb[1]).length())] + String(rgb[1])) + " B" + String(zeroes[3 - (String(rgb[2]).length())] + String(rgb[2]))); //each color is formated with the right amount of zeroes

  //output RGB values
  analogWrite(red, rgb[0]);
  analogWrite(green, rgb[1]);
  analogWrite(blue, rgb[2]);
  
  delay(anim_delay);
}

void breath()
{
  //read and write values
  valRead();
  analogWrite(red, rgb[0]);
  analogWrite(green, rgb[1]);
  analogWrite(blue, rgb[2]);

  //save rgb values for later use
  int beforeRGB[] = {rgb[0], rgb[1], rgb[2]};
  int previousRGB[] = {0, 0, 0};
  //dim down
  while (rgb[0] > 0 || rgb[1] > 0 || rgb[2] > 0)
  {
    for (int j = 0; j < 3; j++)
    {
      // test for button press
      if (digitalRead(button) == LOW)
      {
        break;
      }

      //change RGB values and correct any mistakes
      if (rgb[j] > 0)
      {
        rgb[j] = round(rgb[j] * 0.9);
        if (rgb[j] == previousRGB[j])
        {
          rgb[j]--;
        }
        previousRGB[j] = rgb[j];
      }
      else
      {
        rgb[j] = 0;
      }

      if (rgb[j] < 0)
      {
        rgb[j] = 0;
      }
      else if (rgb[j] > 255)
      {
        rgb[j] = 255;
      }
    }

    //write new RGB values
    analogWrite(red, rgb[0]);
    analogWrite(green, rgb[1]);
    analogWrite(blue, rgb[2]);

    //test for button press
    if (digitalRead(button) == LOW)
    {
      break;
    }
    delay(breathDelay);
  }
  delay(150);

  previousRGB[0] = -1;
  previousRGB[1] = -1;
  previousRGB[2] = -2;
  
  // dim up
  while (rgb[0] < beforeRGB[0] || rgb[1] < beforeRGB[1] || rgb[2] < beforeRGB[2])
  {
    for (int j = 0; j < 3; j++)
    {
      //test for button press
      if (digitalRead(button) == LOW)
      {
        break;
      }

      //change RGB values and correct any mistakes
      if (beforeRGB[j] != 0 && rgb[j] < beforeRGB[j] && rgb[j] < 255)
      {
        rgb[j] = round((rgb[j] * 1.1) + 0.3);
        if (rgb[j] == previousRGB[j])
        {
          rgb[j]++;
        }

        previousRGB[j] = rgb[j];
      }
      else
      {
        rgb[j] = beforeRGB[j];
      }
      if (rgb[j] < 0)
      {
        rgb[j] = 0;
      }
      else if (rgb[j] > 255)
      {
        rgb[j] = 255;
      }
    }
    
    //output new RGB values
    analogWrite(red, rgb[0]);
    analogWrite(green, rgb[1]);
    analogWrite(blue, rgb[2]);

    //test for button press
    if (digitalRead(button) == LOW)
    {
      break;
    }
    delay(breathDelay);
  }
  delay(1500);
}

void valRead()
{
  val = map(analogRead(A0), 0, 1023, 255, 0); //read and map red value
  //correct values
  if (val >= minVal)
  {
    rgb[0] = val;
  }
  else
  {
    rgb[0] = 0;
  }
  val = map(analogRead(A1), 0, 1023, 255, 0);
  if (val >= minVal)
  {
    rgb[1] = val;
  }
  else
  {
    rgb[1] = 0;
  }
  val = map(analogRead(A2), 0, 1023, 255, 0);
  if (val >= minVal)
  {
    rgb[2] = val;
  }
  else
  {
    rgb[2] = 0;
  }
}

// code stored in the sketch: PcRGB_noLCD.ino
//define pins for RGB values output and button
#define red 9
#define green 10
#define blue 11
#define button 7

//define loop variables to use them later inside loops
int i = 0;
int j = 0;

//define variables for mode selection
const int maxMode = 2; //if you add/remove a mode increase/decrease this value
int mode = 0; //By changing this value you change on which mode the controller will start

//define variables for reading RGB values from potentiometer
const int minVal = 2; //below this value 0 is returned as reading
int val; //temporarily stores read vealues
int rgb[] = {000, 000, 000};

//define variables for wheel and breath animations
const float breathPercentage = 0.98; //percentage to increase/decrease breathing smoothness
const int wheelDelay = 10;
const int breathDelay = 50;

void setup()
{
  //set analog pins 1-3 as inputs for the potentiometers
  for (i = 0; i < 3; i++);
  {
    pinMode("A" + i, INPUT);
  }

  //same for digital pins for RGB outputs and button
  pinMode(red, OUTPUT);
  pinMode(green, OUTPUT);
  pinMode(blue, OUTPUT);
  pinMode(button, INPUT_PULLUP);
}
void loop()
{
  //change mode if button pressed
  if (digitalRead(button) == LOW)
  {
    //loop through modes
    if (mode < maxMode)
    {
      mode++;

    }
    else
    {
      mode = 0;
    }

    //signal for mode change
    for (int i = 0; i < 2; i++)
    {
      analogWrite(red, 255);
      analogWrite(green, 0);
      analogWrite(blue, 0);
      delay(500);
      analogWrite(red, 0);
      delay(500);
    }
  }

  //go to selected mode
  if (mode == 0)
  {
    manual();
  }
  else if (mode == 1)
  {
    breath();
  }
  else if (mode == 2)
  {
    colorWheel();
  }
}

//loop through colors (rainbow effect)
void colorWheel()
{
  for (/* no initialization */; rgb[0] >= 0, rgb[2] < 255; rgb[2]++, rgb[0]--) /*red -> blue*/
  {
    for (int j = 0; j < 3; j++)
    {
      if (rgb[j] < 0)
      {
        rgb[j] = 0;
      }
      else if (rgb[j] > 255)
      {
        rgb[j] = 255;
      }
    }
    
    //output RGB values
    analogWrite(red, rgb[0]);
    analogWrite(blue, rgb[2]);
    delay(wheelDelay);

    //test for mode button press
    if (digitalRead(button) == LOW)
    {
      break;
    }
  }

  for (/* no initialization */; rgb[2] >= 0, rgb[1] < 255; rgb[1]++, rgb[2]--) /*blue -> green*/

  {
    for (int j = 0; j < 3; j++)
    {
      if (rgb[j] < 0)
      {
        rgb[j] = 0;
      }
      else if (rgb[j] > 255)
      {
        rgb[j] = 255;
      }
    }
    analogWrite(blue, rgb[2]);
    analogWrite(green, rgb[1]);
    delay(wheelDelay);
    if (digitalRead(button) == LOW)
    {
      break;
    }
  }

  for (/* no initialization */; rgb[1] >= 0, rgb[0] < 255; rgb[0]++, rgb[1]--) /*green -> red*/

  {
    for (int j = 0; j < 3; j++)
    {
      if (rgb[j] < 0)
      {
        rgb[j] = 0;
      }
      else if (rgb[j] > 255)
      {
        rgb[j] = 255;
      }
    }
    analogWrite(red, rgb[0]);
    analogWrite(green, rgb[1]);
    delay(wheelDelay);
    if (digitalRead(button) == LOW)
    {
      break;
    }


  }
}

//changes the color based on the potentiometer input
void manual()
{
  //read values
  valRead();
  
  //output RGB values
  analogWrite(red, rgb[0]);
  analogWrite(green, rgb[1]);
  analogWrite(blue, rgb[2]);
}

void breath()
{
  //read and write values
  valRead();
  analogWrite(red, rgb[0]);
  analogWrite(green, rgb[1]);
  analogWrite(blue, rgb[2]);

  //save rgb values for later use
  int beforeRGB[] = {rgb[0], rgb[1], rgb[2]};
  int previousRGB[] = {0, 0, 0};
  //dim down
  while (rgb[0] > 0 || rgb[1] > 0 || rgb[2] > 0)
  {
    for (int j = 0; j < 3; j++)
    {
      // test for button press
      if (digitalRead(button) == LOW)
      {
        break;
      }

      //change RGB values and correct any mistakes
      if (rgb[j] > 0)
      {
        rgb[j] = round(rgb[j] * 0.9);
        if (rgb[j] == previousRGB[j])
        {
          rgb[j]--;
        }
        previousRGB[j] = rgb[j];
      }
      else
      {
        rgb[j] = 0;
      }

      if (rgb[j] < 0)
      {
        rgb[j] = 0;
      }
      else if (rgb[j] > 255)
      {
        rgb[j] = 255;
      }
    }

    //write new RGB values
    analogWrite(red, rgb[0]);
    analogWrite(green, rgb[1]);
    analogWrite(blue, rgb[2]);

    //test for button press
    if (digitalRead(button) == LOW)
    {
      break;
    }
    delay(breathDelay);
  }
  delay(150);

  previousRGB[0] = -1;
  previousRGB[1] = -1;
  previousRGB[2] = -2;
  
  // dim up
  while (rgb[0] < beforeRGB[0] || rgb[1] < beforeRGB[1] || rgb[2] < beforeRGB[2])
  {
    for (int j = 0; j < 3; j++)
    {
      //test for button press
      if (digitalRead(button) == LOW)
      {
        break;
      }

      //change RGB values and correct any mistakes
      if (beforeRGB[j] != 0 && rgb[j] < beforeRGB[j] && rgb[j] < 255)
      {
        rgb[j] = round((rgb[j] * 1.1) + 0.3);
        if (rgb[j] == previousRGB[j])
        {
          rgb[j]++;
        }

        previousRGB[j] = rgb[j];
      }
      else
      {
        rgb[j] = beforeRGB[j];
      }
      if (rgb[j] < 0)
      {
        rgb[j] = 0;
      }
      else if (rgb[j] > 255)
      {
        rgb[j] = 255;
      }
    }
    
    //output new RGB values
    analogWrite(red, rgb[0]);
    analogWrite(green, rgb[1]);
    analogWrite(blue, rgb[2]);

    //test for button press
    if (digitalRead(button) == LOW)
    {
      break;
    }
    delay(breathDelay);
  }
  delay(1500);
}

void valRead()
{
  val = map(analogRead(A0), 0, 1023, 255, 0); //read and map red value
  //correct values
  if (val >= minVal)
  {
    rgb[0] = val;
  }
  else
  {
    rgb[0] = 0;
  }
  val = map(analogRead(A1), 0, 1023, 255, 0);
  if (val >= minVal)
  {
    rgb[1] = val;
  }
  else
  {
    rgb[1] = 0;
  }
  val = map(analogRead(A2), 0, 1023, 255, 0);
  if (val >= minVal)
  {
    rgb[2] = val;
  }
  else
  {
    rgb[2] = 0;
  }
}

// code stored in the sketch: PcRGB_noLCD_noPotentiometers.ino
//define pins for RGB values output and button
#define red 9
#define green 10
#define blue 11
#define button 7

//define loop variables to use them later inside loops
int i = 0;
int j = 0;

//define variables for mode selection
const int maxMode = 1; //if you add/remove a mode increase/decrease this value
int mode = 0; //By changing this value you change on which mode the controller will start

//define variables for wheel and breath animations
const float breathPercentage = 0.98; //percentage to increase/decrease breathing smoothness
const int wheelDelay = 10;
const int breathDelay = 50;

int rgb[] = {000, 000, 000};

void setup()
{
  //same for digital pins for RGB outputs and button
  pinMode(red, OUTPUT);
  pinMode(green, OUTPUT);
  pinMode(blue, OUTPUT);
  pinMode(button, INPUT_PULLUP);
}
void loop()
{
  //change mode if button pressed
  if (digitalRead(button) == LOW)
  {
    //loop through modes
    if (mode < maxMode)
    {
      mode++;

    }
    else
    {
      mode = 0;
    }

    //signal for mode change
    for (int i = 0; i < 2; i++)
    {
      analogWrite(red, 255);
      analogWrite(green, 0);
      analogWrite(blue, 0);
      delay(500);
      analogWrite(red, 0);
      delay(500);
    }
  }

  //go to selected mode
  if (mode == 0)
  {
    breath();
  }
  else if (mode == 1)
  {
    colorWheel();
  }
}

//loop through colors (rainbow effect)
void colorWheel()
{
  for (/* no initialization */; rgb[0] >= 0, rgb[2] < 255; rgb[2]++, rgb[0]--) /*red -> blue*/
  {
    for (int j = 0; j < 3; j++)
    {
      if (rgb[j] < 0)
      {
        rgb[j] = 0;
      }
      else if (rgb[j] > 255)
      {
        rgb[j] = 255;
      }
    }
    
    //output RGB values
    analogWrite(red, rgb[0]);
    analogWrite(blue, rgb[2]);
    delay(wheelDelay);

    //test for mode button press
    if (digitalRead(button) == LOW)
    {
      break;
    }
  }

  for (/* no initialization */; rgb[2] >= 0, rgb[1] < 255; rgb[1]++, rgb[2]--) /*blue -> green*/

  {
    for (int j = 0; j < 3; j++)
    {
      if (rgb[j] < 0)
      {
        rgb[j] = 0;
      }
      else if (rgb[j] > 255)
      {
        rgb[j] = 255;
      }
    }
    analogWrite(blue, rgb[2]);
    analogWrite(green, rgb[1]);
    delay(wheelDelay);
    if (digitalRead(button) == LOW)
    {
      break;
    }
  }

  for (/* no initialization */; rgb[1] >= 0, rgb[0] < 255; rgb[0]++, rgb[1]--) /*green -> red*/

  {
    for (int j = 0; j < 3; j++)
    {
      if (rgb[j] < 0)
      {
        rgb[j] = 0;
      }
      else if (rgb[j] > 255)
      {
        rgb[j] = 255;
      }
    }
    analogWrite(red, rgb[0]);
    analogWrite(green, rgb[1]);
    delay(wheelDelay);
    if (digitalRead(button) == LOW)
    {
      break;
    }
  }
}

void breath()
{
  int rgb[] = {255, 255, 255}; //define breath color
  analogWrite(red, rgb[0]);
  analogWrite(green, rgb[1]);
  analogWrite(blue, rgb[2]);

  //save rgb values for later use
  int beforeRGB[] = {rgb[0], rgb[1], rgb[2]};
  int previousRGB[] = {0, 0, 0};
  //dim down
  while (rgb[0] > 0 || rgb[1] > 0 || rgb[2] > 0)
  {
    for (int j = 0; j < 3; j++)
    {
      // test for button press
      if (digitalRead(button) == LOW)
      {
        break;
      }

      //change RGB values and correct any mistakes
      if (rgb[j] > 0)
      {
        rgb[j] = round(rgb[j] * 0.9);
        if (rgb[j] == previousRGB[j])
        {
          rgb[j]--;
        }
        previousRGB[j] = rgb[j];
      }
      else
      {
        rgb[j] = 0;
      }

      if (rgb[j] < 0)
      {
        rgb[j] = 0;
      }
      else if (rgb[j] > 255)
      {
        rgb[j] = 255;
      }
    }

    //write new RGB values
    analogWrite(red, rgb[0]);
    analogWrite(green, rgb[1]);
    analogWrite(blue, rgb[2]);

    //test for button press
    if (digitalRead(button) == LOW)
    {
      break;
    }
    delay(breathDelay);
  }
  delay(150);

  previousRGB[0] = -1;
  previousRGB[1] = -1;
  previousRGB[2] = -2;
  
  // dim up
  while (rgb[0] < beforeRGB[0] || rgb[1] < beforeRGB[1] || rgb[2] < beforeRGB[2])
  {
    for (int j = 0; j < 3; j++)
    {
      //test for button press
      if (digitalRead(button) == LOW)
      {
        break;
      }

      //change RGB values and correct any mistakes
      if (beforeRGB[j] != 0 && rgb[j] < beforeRGB[j] && rgb[j] < 255)
      {
        rgb[j] = round((rgb[j] * 1.1) + 0.3);
        if (rgb[j] == previousRGB[j])
        {
          rgb[j]++;
        }

        previousRGB[j] = rgb[j];
      }
      else
      {
        rgb[j] = beforeRGB[j];
      }
      if (rgb[j] < 0)
      {
        rgb[j] = 0;
      }
      else if (rgb[j] > 255)
      {
        rgb[j] = 255;
      }
    }
    
    //output new RGB values
    analogWrite(red, rgb[0]);
    analogWrite(green, rgb[1]);
    analogWrite(blue, rgb[2]);

    //test for button press
    if (digitalRead(button) == LOW)
    {
      break;
    }
    delay(breathDelay);
  }
  delay(1500);
}

// code stored in the sketch: PcRGB_singleMode.ino
//define pins for RGB values output and button
#define red 9
#define green 10
#define blue 11
#define button 7

//define loop variables to use them later inside loops
int i = 0;
int j = 0;

//define variables for mode selection
int mode = 0; //By changing this value you change on which mode the controller will start

//define variables for wheel and breath animations
const float breathPercentage = 0.98; //percentage to increase/decrease breathing smoothness
const int wheelDelay = 10;
const int breathDelay = 50;

int rgb[] = {000, 000, 000};

void setup()
{
  //same for digital pins for RGB outputs and button
  pinMode(red, OUTPUT);
  pinMode(green, OUTPUT);
  pinMode(blue, OUTPUT);
  pinMode(button, INPUT_PULLUP);
}
void loop()
{
  //go to selected mode
  if (mode == 0)
  {
    breath();
  }
  else if (mode == 1)
  {
    colorWheel();
  }
}

//loop through colors (rainbow effect)
void colorWheel()
{
  for (/* no initialization */; rgb[0] >= 0, rgb[2] < 255; rgb[2]++, rgb[0]--) /*red -> blue*/
  {
    for (int j = 0; j < 3; j++)
    {
      if (rgb[j] < 0)
      {
        rgb[j] = 0;
      }
      else if (rgb[j] > 255)
      {
        rgb[j] = 255;
      }
    }
    
    //output RGB values
    analogWrite(red, rgb[0]);
    analogWrite(blue, rgb[2]);
    delay(wheelDelay);

    //test for mode button press
    if (digitalRead(button) == LOW)
    {
      break;
    }
  }

  for (/* no initialization */; rgb[2] >= 0, rgb[1] < 255; rgb[1]++, rgb[2]--) /*blue -> green*/

  {
    for (int j = 0; j < 3; j++)
    {
      if (rgb[j] < 0)
      {
        rgb[j] = 0;
      }
      else if (rgb[j] > 255)
      {
        rgb[j] = 255;
      }
    }
    analogWrite(blue, rgb[2]);
    analogWrite(green, rgb[1]);
    delay(wheelDelay);
    if (digitalRead(button) == LOW)
    {
      break;
    }
  }

  for (/* no initialization */; rgb[1] >= 0, rgb[0] < 255; rgb[0]++, rgb[1]--) /*green -> red*/

  {
    for (int j = 0; j < 3; j++)
    {
      if (rgb[j] < 0)
      {
        rgb[j] = 0;
      }
      else if (rgb[j] > 255)
      {
        rgb[j] = 255;
      }
    }
    analogWrite(red, rgb[0]);
    analogWrite(green, rgb[1]);
    delay(wheelDelay);
    if (digitalRead(button) == LOW)
    {
      break;
    }
  }
}

void breath()
{
  int rgb[] = {255, 255, 255}; //define breath color
  analogWrite(red, rgb[0]);
  analogWrite(green, rgb[1]);
  analogWrite(blue, rgb[2]);

  //save rgb values for later use
  int beforeRGB[] = {rgb[0], rgb[1], rgb[2]};
  int previousRGB[] = {0, 0, 0};
  //dim down
  while (rgb[0] > 0 || rgb[1] > 0 || rgb[2] > 0)
  {
    for (int j = 0; j < 3; j++)
    {
      // test for button press
      if (digitalRead(button) == LOW)
      {
        break;
      }

      //change RGB values and correct any mistakes
      if (rgb[j] > 0)
      {
        rgb[j] = round(rgb[j] * 0.9);
        if (rgb[j] == previousRGB[j])
        {
          rgb[j]--;
        }
        previousRGB[j] = rgb[j];
      }
      else
      {
        rgb[j] = 0;
      }

      if (rgb[j] < 0)
      {
        rgb[j] = 0;
      }
      else if (rgb[j] > 255)
      {
        rgb[j] = 255;
      }
    }

    //write new RGB values
    analogWrite(red, rgb[0]);
    analogWrite(green, rgb[1]);
    analogWrite(blue, rgb[2]);

    //test for button press
    if (digitalRead(button) == LOW)
    {
      break;
    }
    delay(breathDelay);
  }
  delay(150);

  previousRGB[0] = -1;
  previousRGB[1] = -1;
  previousRGB[2] = -2;
  
  // dim up
  while (rgb[0] < beforeRGB[0] || rgb[1] < beforeRGB[1] || rgb[2] < beforeRGB[2])
  {
    for (int j = 0; j < 3; j++)
    {
      //test for button press
      if (digitalRead(button) == LOW)
      {
        break;
      }

      //change RGB values and correct any mistakes
      if (beforeRGB[j] != 0 && rgb[j] < beforeRGB[j] && rgb[j] < 255)
      {
        rgb[j] = round((rgb[j] * 1.1) + 0.3);
        if (rgb[j] == previousRGB[j])
        {
          rgb[j]++;
        }

        previousRGB[j] = rgb[j];
      }
      else
      {
        rgb[j] = beforeRGB[j];
      }
      if (rgb[j] < 0)
      {
        rgb[j] = 0;
      }
      else if (rgb[j] > 255)
      {
        rgb[j] = 255;
      }
    }
    
    //output new RGB values
    analogWrite(red, rgb[0]);
    analogWrite(green, rgb[1]);
    analogWrite(blue, rgb[2]);

    //test for button press
    if (digitalRead(button) == LOW)
    {
      break;
    }
    delay(breathDelay);
  }
  delay(1500);
}
